# Fritzing sketch Circuit (saved by Fritzing 0.9.4)
breadboards: 1

parts:
  M1 = DOIT Esp32 DevKit v1 (30 pins long, 11 pins width) [part_number=ESP32S-PIN30]
  Part1 = InvenSense MPU6050
  Part2 = DHT22 module
  LED1 = smd LED [color="Green (560nm)" package="0603 [SMD]"]
  R1 = Resistor [tolerance=±5% resistance=220 package="2010 [SMD]"]
  L1 = sct-013 [part_number=sct-013 package="4Ucon 08780 [THT]"]  # not connected
  TRS1 = Audio Jack (TRS) 3.5mm [package="4Ucon 08780 [THT]"]
  R2 = Resistor [tolerance=±5% resistance=100k package="2010 [SMD]"]
  R3 = Resistor [tolerance=±5% resistance=100k package="2010 [SMD]"]
  C1 = Capacitor Polarized [package=cpol-radial-10uf-25v]

nets:
  3V3: M1.3V3, Part1.VCC, R2.Pin_1
  GND: M1.GND, Part1.GND, Part2.GND, R3.Pin_0, C1.-
  N1: M1.D2, R1.Pin_1
  N2: M1.D21, Part1.SDA
  N3: M1.D22, Part1.SCL
  N4: M1.D23, Part2.DATA
  N5: M1.D34, TRS1.Tip
  VIN: M1.VIN, Part2.VCC, LED1.cathode
  N6: LED1.anode, R1.Pin_0
  N7: TRS1.Sleeve, R2.Pin_0, R3.Pin_1, C1.+

custom parts:
  DOIT Esp32 DevKit v1 (30 pins long, 11 pins width): The DOIT Esp32 DevKit v1 is one of the development board created by DOIT to evaluate the ESP-WROOM-32 module. It is based on the ESP32 microcontroller that boasts Wifi, Bluetooth, Ethernet and Low Power support all in a single chip. (vanepp) made breadboard work, adjusted pin numbering and labels and reduced size of schematic and cleaned up pcb. This chip is 30pins long (2 x15) and 11 pins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
  sct-013: sct-013 Current transformer. The pcb footprint is from the 3.5mm stereo jack (as the sensor comes with a 3.5 mm stero plug).
